// Digital circuit main.dig as structural Verilog
module main (
  input  clk,
  input  [3:0] in_2,
  input  in_5,
  input  in_6,
  output out_3,
  output [7:0] out_4
);

  DipSwitch F1 (.out(out_4[0]));
  DipSwitch F2 (.out(out_4[1]));
  DipSwitch F3 (.out(out_4[2]));
  DipSwitch F4 (.out(out_4[3]));
  // ComPort #(.comPort("COM6")) comport_1: pin names not known; wires that end beside it: {in_2, out_4[3:0]}, in_5, in_6, clk, out_3

  assign out_4[7:4] = in_2;

  // Notes on the sheet:
  //   clk: Hz: 2
endmodule
